// Logisim project P1-fulladder-.circ as structural Verilog: 1 circuit, main circuit main
module main (
  input  An,
  input  Bn,
  input  Cn_1,
  output sum,
  output CARRY
);

  wire and_1_out, and_2_out, and_3_out, and_4_out, and_5_out, and_6_out, not_1_out, not_2_out, not_3_out,
       not_4_out, or_1_out;

  not not_1 (not_1_out, An);
  and and_1 (and_1_out, not_1_out, Bn);
  and and_2 (and_2_out, An, not_2_out);
  not not_2 (not_2_out, Bn);
  or or_1 (or_1_out, and_1_out, and_2_out);
  and and_3 (and_3_out, or_1_out, Cn_1);
  and and_4 (and_4_out, An, Bn);
  not not_3 (not_3_out, or_1_out);
  and and_5 (and_5_out, not_3_out, Cn_1);
  and and_6 (and_6_out, or_1_out, not_4_out);
  not not_4 (not_4_out, Cn_1);
  or or_2 (CARRY, and_3_out, and_4_out);
  or or_3 (sum, and_5_out, and_6_out);

  // Notes on the sheet:
  //   Full-Adder using basic gates 
  //   An
  //   0
  //   0
  //   0
  //   0
  //   1
  //   1
  //   1
  //   1
  //   Bn
  //   0
  //   0
  //   1
  //   1
  //   0
  //   0
  //   1
  //   1
  //   Cn-1
  //   0
  //   1
  //   0
  //   1
  //   0
  //   1
  //   0
  //   1
  //   Sum
  //   0
  //   1
  //   1
  //   0
  //   1
  //   0
  //   0
  //   1
  //   Carry
  //   0
  //   0
  //   0
  //   1
  //   0
  //   1
  //   1
  //   1
endmodule
