// Logisim project P10-2 to 4 dec_using_BG.circ as structural Verilog: 1 circuit, main circuit main
module main (
  input  in_1,
  input  in_2,
  output out_3,
  output out_4,
  output out_5,
  output out_6
);

  wire not_1_out, not_2_out;

  not not_1 (not_1_out, in_1);
  not not_2 (not_2_out, in_2);
  and and_1 (out_3, in_2, in_1);
  and and_2 (out_4, in_1, not_2_out);
  and and_3 (out_5, in_2, not_1_out);
  and and_4 (out_6, not_2_out, not_1_out);

  // Notes on the sheet:
  //   implement of 2 to 4 decoder using basic gates
  //   s0
  //   s1
  //   0
  //   0
  //   0
  //   1
  //   1
  //   0
  //   1
  //   1
  //   q0
  //   1
  //   0
  //   0
  //   0
  //   q1
  //   0
  //   1
  //   0
  //   0
  //   q2
  //   0
  //   0
  //   1
  //   0
  //   q3
  //   0
  //   0
  //   0
  //   1
endmodule
