// Logisim project P11-counter _ register.circ as structural Verilog: 1 circuit, main circuit main
module main (
  input  load,
  input  [3:0] s3_s2_s1_s0,
  input  cout,
  input  clk,
  input  clr,
  input  [3:0] s3_s2_s1_s0_2,
  input  en,
  input  clr_2,
  input  clk_2,
  output [3:0] q3_q2_q1_q0,
  output ca,
  output [3:0] q3_q2_q1_q0_2
);

  Counter #(.width(4), .max('hf)) counter_1 (
    .load(load), .D(s3_s2_s1_s0), .count(cout), .Q(q3_q2_q1_q0), .carry(ca), .clk(clk), .clr(clr));
  Register #(.width(4)) register_1 (.D(s3_s2_s1_s0_2), .en(en), .Q(q3_q2_q1_q0_2), .clk(clk_2), .clr(clr_2));

  // Notes on the sheet:
  //   Counter
  //   Register
endmodule
