// Logisim project P12-D-filp _flop.circ as structural Verilog: 1 circuit, main circuit main
module main (
  input  clk,
  input  d0,
  input  d1,
  input  d2,
  input  d3,
  output q0,
  output q1,
  output q2,
  output q3
);

  D_Flip_Flop d_ff_1 (.clk(clk), .D(d0), .Q(q0));  // open: Qn, preset, en, reset
  D_Flip_Flop d_ff_2 (.clk(clk), .D(d1), .Q(q1));  // open: Qn, preset, en, reset
  D_Flip_Flop d_ff_3 (.clk(clk), .D(d2), .Q(q2));  // open: Qn, preset, en, reset
  D_Flip_Flop d_ff_4 (.clk(clk), .D(d3), .Q(q3));  // open: Qn, preset, en, reset

  // Notes on the sheet:
  //   4 bit basic register D filp - flop 
endmodule
