// Logisim project P2-fulladder.circ as structural Verilog: 1 circuit, main circuit main
module main (
  input  An,
  input  Bn,
  input  Cn_1,
  output SUM,
  output CARRY
);

  wire and_2_out, and_out, xor_2_out, xor_out;

  xor \xor  (xor_out, An, Bn);
  xor xor_2 (xor_2_out, An, Bn);
  and \and  (and_out, xor_2_out, Cn_1);
  and and_2 (and_2_out, An, Bn);
  xor XOR_3 (SUM, xor_out, Cn_1);
  or \or  (CARRY, and_out, and_2_out);

  // Notes on the sheet:
  //   Full-Adder using XOR gates 
  //   An
  //   0
  //   0
  //   0
  //   0
  //   1
  //   1
  //   1
  //   1
  //   Bn
  //   0
  //   0
  //   1
  //   1
  //   0
  //   0
  //   1
  //   1
  //   Cn-1
  //   0
  //   1
  //   0
  //   1
  //   0
  //   1
  //   0
  //   1
  //   Sum
  //   0
  //   1
  //   1
  //   0
  //   1
  //   0
  //   0
  //   1
  //   Carry
  //   0
  //   0
  //   0
  //   1
  //   0
  //   1
  //   1
  //   1
endmodule
