// Logisim project P3-Half-Adder.circ as structural Verilog: 1 circuit, main circuit main
module main (
  input  A,
  input  B,
  input  A_2,
  input  B_2,
  output SUM,
  output CARRY,
  output sum___a_prime_b_ab_prime,
  output carry_ab
);

  wire A_prime_B_out, AB_prime_out, INV_2_out, INV_out;

  not INV (INV_out, A);
  not INV_2 (INV_2_out, B);
  and A_prime_B (A_prime_B_out, INV_out, B);
  and AB_prime (AB_prime_out, A, INV_2_out);
  and AB (CARRY, A, B);
  xor \xor  (sum___a_prime_b_ab_prime, A_2, B_2);
  and AB_2 (carry_ab, A_2, B_2);
  or A_prime_B_AB_prime (SUM, A_prime_B_out, AB_prime_out);

  // Notes on the sheet:
  //   half adder using basic gates 
  //   Half adder using XOR gates 
  //   a
  //   0
  //   0
  //   1
  //   1
  //   b
  //   0
  //   1
  //   0
  //   1
  //   sum
  //   0
  //   1
  //   1
  //   0
  //   carry
  //   0
  //   0
  //   0
  //   1
endmodule
