// Logisim project P4-mux 2in1.circ as structural Verilog: 1 circuit, main circuit main
module main (
  input  S,
  input  D1,
  input  D0,
  output F___SD1___S_prime_D0
);

  wire and_2_out, and_out, not_1_out;

  not not_1 (not_1_out, S);
  and \and  (and_out, S, D1);
  and and_2 (and_2_out, not_1_out, D0);
  or \or  (F___SD1___S_prime_D0, and_out, and_2_out);

  // Notes on the sheet:
  //   2) MUX 2*1 using basic gates
  //   s
  //   0
  //   0
  //   0
  //   0
  //   1
  //   1
  //   1
  //   1
  //   D1
  //   0
  //   0
  //   1
  //   1
  //   0
  //   0
  //   1
  //   1
  //   D2
  //   0
  //   1
  //   0
  //   1
  //   0
  //   1
  //   0
  //   1
  //   F
  //   0
  //   1
  //   0
  //   1
  //   0
  //   0
  //   1
  //   1
endmodule
