// Logisim project P5-MUX4in1 BG.circ as structural Verilog: 1 circuit, main circuit main
module main (
  input  S1,
  input  S0,
  input  D3,
  input  D2,
  input  D1,
  input  D0,
  output F__s1_prime_s0_prime___s1_prime_s0d1___s1s0_prime_d2___s1s0d3
);

  wire AND_2_out, AND_3_out, ANd_4_out, AND_out, not_1_out, not_2_out;

  not not_1 (not_1_out, S1);
  not not_2 (not_2_out, S0);
  and AND (AND_out, S1, S0, D3);
  and AND_2 (AND_2_out, S1, not_2_out, D2);
  and AND_3 (AND_3_out, not_1_out, S0, D1);
  and ANd_4 (ANd_4_out, not_1_out, not_2_out, D0);
  or OR (F__s1_prime_s0_prime___s1_prime_s0d1___s1s0_prime_d2___s1s0d3, AND_out, AND_2_out, AND_3_out, ANd_4_out);

  // Notes on the sheet:
  //   3) MUX 4*1 using basic gates
  //   s1
  //   0
  //   0
  //   1
  //   1
  //   s2
  //   0
  //   1
  //   0
  //   1
  //   F
  //   D0
  //   D1
  //   D2
  //   D3
endmodule
