// Logisim project P6-Mux_usingPlexer.circ as structural Verilog: 1 circuit, main circuit main
module main (
  input  D0,
  input  D1,
  input  EN,
  input  S,
  input  D0_2,
  input  D1_2,
  input  D2,
  input  D3,
  input  [1:0] in_9,
  input  EN_2,
  output F___SD1___S_prime_D0,
  output F__s1_prime_s0_prime___s1_prime_s0d1___s1s0_prime_d2___s1s0d3
);

  Multiplexer multiplexer_1 (.in0(D0), .in1(D1), .out(F___SD1___S_prime_D0), .sel(S), .en(EN));
  Multiplexer #(.select(2)) multiplexer_2 (
    .in0(D0_2), .in1(D1_2), .in2(D2), .in3(D3),
    .out(F__s1_prime_s0_prime___s1_prime_s0d1___s1s0_prime_d2___s1s0d3), .sel(in_9), .en(EN_2));

  // Notes on the sheet:
  //   MUX 2 in 1 using plexer
  //   MUX 4 in 1 using plexer
  //   s
  //   0
  //   0
  //   s'
  //   0
  //   1
  //   0
  //   0
  //   1
  //   1
  //   F
  //   D0
  //   D1
  //   s
  //   s'
  //   0
  //   1
  //   0
  //   1
  //   f
  //   D0
  //   D1
  //   D2
  //   D3
endmodule
