// Logisim project P7-2 to 4 decoder U-Plewcer.circ as structural Verilog: 1 circuit, main circuit main
module main (
  input  EN,
  input  [1:0] S1__S0,
  output D0__S0_prime_S1_prime,
  output D1_S0_S1_prime,
  output D2_S0_prime_S1,
  output D3_S0_S1
);

  Decoder #(.select(2)) decoder_1 (
    .out0(D0__S0_prime_S1_prime), .out1(D1_S0_S1_prime), .out2(D2_S0_prime_S1), .out3(D3_S0_S1),
    .sel(S1__S0), .en(EN));

  // Notes on the sheet:
  //   2 to 4 decoder using plexer
  //   s0
  //   0
  //   0
  //   1
  //   1
  //   s1
  //   0
  //   1
  //   0
  //   1
  //   f
  //   D0
  //   D1
  //   D2
  //   D3
endmodule
