// Logisim project P8-4 to 16 decoder.circ as structural Verilog: 1 circuit, main circuit main
module main (
  input  [1:0] s0___s1,
  input  EN,
  input  [1:0] S3__S2,
  output D0__S0_prime_S1_prime_S2_prime_S3_prime,
  output D1_S0_prime_S1_prime_S2_prime_S3,
  output D2,
  output D3,
  output D4,
  output D5,
  output D6,
  output D7,
  output D8,
  output D9,
  output D10,
  output D11,
  output D12,
  output D13,
  output D14,
  output D15
);

  wire decoder_1_out0, decoder_1_out1, decoder_1_out2, decoder_1_out3;

  Decoder #(.select(2)) decoder_1 (
    .out0(decoder_1_out0), .out1(decoder_1_out1), .out2(decoder_1_out2), .out3(decoder_1_out3), .sel(S3__S2),
    .en(EN));
  Decoder #(.select(2)) decoder_2 (
    .out0(D0__S0_prime_S1_prime_S2_prime_S3_prime), .out1(D1_S0_prime_S1_prime_S2_prime_S3), .out2(D2),
    .out3(D3), .sel(s0___s1), .en(decoder_1_out0));
  Decoder #(.select(2)) decoder_3 (.out0(D4), .out1(D5), .out2(D6), .out3(D7), .sel(s0___s1), .en(decoder_1_out1));
  Decoder #(.select(2)) decoder_4 (.out0(D8), .out1(D9), .out2(D10), .out3(D11), .sel(s0___s1), .en(decoder_1_out2));
  Decoder #(.select(2)) decoder_5 (.out0(D12), .out1(D13), .out2(D14), .out3(D15), .sel(s0___s1), .en(decoder_1_out3));

  // Notes on the sheet:
  //   4 to 16 decoder 
endmodule
