// Logisim project P9-full adder by decoder.circ as structural Verilog: 1 circuit, main circuit main
module main (
  input  En,
  input  [2:0] x_y_z,
  output S___d1___d2___d3___d7,
  output C___d3__d5__d6__d7
);

  wire demultiplexer_1_out0, demultiplexer_1_out1, demultiplexer_1_out2, demultiplexer_1_out3,
       demultiplexer_1_out4, demultiplexer_1_out5, demultiplexer_1_out6, demultiplexer_1_out7;

  Demultiplexer #(.select(3)) demultiplexer_1 (
    .out0(demultiplexer_1_out0), .out1(demultiplexer_1_out1), .out2(demultiplexer_1_out2),
    .out3(demultiplexer_1_out3), .out4(demultiplexer_1_out4), .out5(demultiplexer_1_out5),
    .out6(demultiplexer_1_out6), .out7(demultiplexer_1_out7), .sel(x_y_z), .en(En));  // open: in
  or or_1 (S___d1___d2___d3___d7, demultiplexer_1_out1, demultiplexer_1_out2, demultiplexer_1_out4, demultiplexer_1_out7);
  or or_2 (C___d3__d5__d6__d7, demultiplexer_1_out3, demultiplexer_1_out5, demultiplexer_1_out6, demultiplexer_1_out7);

  // Notes on the sheet:
  //   Full adder by decoder 
  //   x
  //   0
  //   0
  //   0
  //   0
  //   1
  //   1
  //   1
  //   1
  //   y
  //   0
  //   0
  //   1
  //   1
  //   0
  //   0
  //   1
  //   1
  //   z
  //   0
  //   1
  //   0
  //   1
  //   0
  //   1
  //   0
  //   1
  //   sum
  //   carry
endmodule
