// Logisim project PRO.circ as structural Verilog: 1 circuit, main circuit main
module main (
  input  [7:0] X,
  input  [7:0] Y,
  output S0,
  output S1,
  output S2,
  output S3
);

  wire not_1_out;

  not not_1 (not_1_out, Y[1]);
  Multiplexer #(.select(2)) multiplexer_1 (.in1(not_1_out), .in2(Y[2]));  // open: in0, in3, out, sel, en
endmodule
