// Logisim project project1.0.circ as structural Verilog: 1 circuit, main circuit main
// 00
module main (
  input  [3:0] S0_S1_S2_S3,
  input  [7:0] X,
  input  [7:0] Y,
  input  [7:0] F,
  output V,
  output N,
  output C,
  output Z
);

  wire and_2_out, and_3_out, not_3_out, not_4_out, not_5_out;
  wire [6:0] adder_1_out;
  wire [7:0] and_1_out, multiplexer_1_out, multiplexer_2_out, not_1_out, not_2_out, or_1_out, xor_1_out;

  assign and_1_out = X & Y;  // AND_Gate and_1, 8 bits wide
  assign or_1_out = X | Y;  // OR_Gate or_1, 8 bits wide
  assign xor_1_out = X ^ Y;  // XOR_Gate xor_1, 8 bits wide
  assign not_1_out = ~X;  // NOT_Gate not_1, 8 bits wide
  assign not_2_out = ~Y;  // NOT_Gate not_2, 8 bits wide
  Multiplexer #(.select(2), .width(8)) multiplexer_1 (
    .in0({8{1'b0}}), .in1(not_2_out), .in2(Y), .in3({8{1'b1}}), .out(multiplexer_1_out),
    .sel(S0_S1_S2_S3[2:1]));  // open: en
  Adder adder_1 (.a(X), .b(multiplexer_1_out), .out({N, adder_1_out}), .cin(S0_S1_S2_S3[0]), .cout(C));
  Multiplexer #(.select(3), .width(8)) multiplexer_2 (
    .in0(and_1_out), .in1(or_1_out), .in2(xor_1_out), .in3(not_1_out), .in4({Y[6:0], Y[7]}), .in5(Y),
    .in6({Y[6:0], Y[7]}), .out(multiplexer_2_out), .en(S0_S1_S2_S3[0]));  // open: in7, sel
  Multiplexer #(.width(8)) multiplexer_3 (
    .in0({N, adder_1_out}), .in1(multiplexer_2_out), .out(F), .sel(S0_S1_S2_S3[3]));  // open: en
  and and_2 (and_2_out, multiplexer_1_out[7], X[7], not_3_out);
  not not_3 (not_3_out, N);
  not not_4 (not_4_out, X[7]);
  not not_5 (not_5_out, multiplexer_1_out[7]);
  and and_3 (and_3_out, not_4_out, not_5_out, N);
  or or_2 (V, and_2_out, and_3_out);
  nor nor_1 (Z, F[0], F[1], F[2], F[3], F[4], F[5], F[6], F[7]);
endmodule
